# Fritzing sketch main (saved by Fritzing 0.9.3b)
breadboards: 1

parts:
  Arduino = Arduino Nano (Rev3.0)
  BMP180 = Barometric Pressure Sensor - BMP180 Breakout (GY-68)
  DHT22 = Humidity and Temperature Sensor RHT03
  RTC = ZS-042 RTC Module
  BTLE = Bluetooth HC-05 Macho

nets:
  GND: Arduino.GND, BMP180.GND, DHT22.GND_2, RTC.GND, BTLE.GND
  N1: Arduino.D2, DHT22.Data-signal
  N2: Arduino.D8, BTLE.TXD
  N3: Arduino.D9, BTLE.RXD
  5V: Arduino.5V, RTC.VCC
  N4: Arduino.A5, BMP180.SCL, RTC.SCL
  N5: Arduino.A4, BMP180.SDA, RTC.SDA
  VCC: Arduino.3V3, BMP180.VCC, DHT22.Vcc, BTLE.VCC
